// Logisim project ch17.circ as structural Verilog
module fadder (
  input  a,
  input  b,
  input  c,
  output sum,
  output carry
);

  wire ab_out, ac_out, bc_out;

  xor xor_1 (sum, a, b, c);
  and ab (ab_out, a, b);
  and ac (ac_out, a, c);
  and bc (bc_out, b, c);
  or or_1 (carry, ab_out, ac_out, bc_out);
endmodule

module fourbit (
  input  a0,
  input  b0,
  input  a1,
  input  b1,
  input  a2,
  input  b2,
  input  a3,
  input  b3,
  output s0,
  output s1,
  output s2,
  output s3,
  output cout
);

  wire f0_carry, f1_carry, f2_carry;

  fadder f0 (.a(a0), .b(b0), .sum(s0), .carry(f0_carry));  // open: c
  fadder f1 (.a(a1), .b(b1), .c(f0_carry), .sum(s1), .carry(f1_carry));
  fadder f2 (.a(a2), .b(b2), .c(f1_carry), .sum(s2), .carry(f2_carry));
  fadder f3 (.a(a3), .b(b3), .c(f2_carry), .sum(s3), .carry(cout));
endmodule

module signed_adder (
  input  cin,
  input  a,
  input  b,
  input  b_inv,
  output s,
  output c
);

  wire multiplexer_1_out, not_1_out;

  Multiplexer multiplexer_1 (.in0(b), .in1(not_1_out), .out(multiplexer_1_out), .sel(b_inv));
  not not_1 (not_1_out, b);
  fadder fadder_1 (.a(a), .b(multiplexer_1_out), .c(cin), .sum(s), .carry(c));

  // Notes on the sheet:
  //   modify the circuit so it can also compute b-a
  //   hook four of these together to make an adder that can compute a+b a-b
endmodule

module signed_fourbit_adder (
  input  binv,
  input  cin,
  input  a0,
  input  b0,
  input  a1,
  input  b1,
  input  a2,
  input  b2,
  input  a3,
  input  b3,
  output s0,
  output s1,
  output s2,
  output s3,
  output cout
);

  wire add0_c, add1_c, add2_c;

  signed_adder add0 (.cin(cin), .a(a0), .b(b0), .b_inv(binv), .s(s0), .c(add0_c));
  signed_adder add1 (.cin(add0_c), .a(a1), .b(b1), .b_inv(binv), .s(s1), .c(add1_c));
  signed_adder add2 (.cin(add1_c), .a(a2), .b(b2), .b_inv(binv), .s(s2), .c(add2_c));
  signed_adder add3 (.cin(add2_c), .a(a3), .b(b3), .b_inv(binv), .s(s3), .c(cout));
endmodule

module Rs_flip_flop (
  input  R,
  input  S,
  input  Reset,
  input  clk,
  input  Set,
  input  in_6,
  input  in_7,
  input  in_8,
  input  in_9,
  input  clock,
  input  enable,
  input  clear,
  output Q,
  output QBAR,
  output Q1,
  output Q1bar,
  output out_17,
  output out_18
);

  wire and_1_out, and_2_out;

  S_R_Flip_Flop s_r_ff_1 (.S(in_7), .R(in_8), .clk(clock), .Q(out_17), .reset(in_9), .Qn(out_18), .preset(in_6));
  and and_1 (and_1_out, Reset, clk);
  and and_2 (and_2_out, clk, Set);
  nor nor_1 (Q, R, QBAR);
  nor nor_2 (QBAR, Q, S);
  // Digital_Oscilloscope digital_oscilloscope_1: pin names not known; wires that end beside it: clock, in_8, in_7, out_17, enable, clear
  nor nor_3 (Q1, and_1_out, Q1bar);
  nor nor_4 (Q1bar, Q1, and_2_out);

  // Notes on the sheet:
  //   RS FLIP FLOP
  //   RS Flip Flop with a clk( hold that bit)
endmodule

module D_latch (
  input  data,
  input  clk,
  output Q1,
  output Q1bar
);

  wire and_1_out, and_2_out;

  and and_1 (and_1_out, ~data, clk);  // AND_Gate
  and and_2 (and_2_out, clk, data);
  nor nor_1 (Q1, and_1_out, Q1bar);
  nor nor_2 (Q1bar, Q1, and_2_out);

  // Notes on the sheet:
  //   Level triiggered D latch
endmodule

module D_latch_edge_triggered (
  input  data,
  input  clk,
  input  enable,
  input  clear,
  output out_5
);

  wire d_latch_1_q1, not_1_out;

  not not_1 (not_1_out, clk);
  D_latch d_latch_1 (.data(data), .clk(not_1_out), .Q1(d_latch_1_q1));  // open: Q1bar
  // Digital_Oscilloscope digital_oscilloscope_1: pin names not known; wires that end beside it: clk, data, out_5, enable, clear
  D_latch d_latch_2 (.data(d_latch_1_q1), .clk(clk), .Q1(out_5));  // open: Q1bar
endmodule

module four_bit_latch (
  input  d3,
  input  d2,
  input  d1,
  input  d0,
  input  set,
  input  clk,
  input  reset,
  output q3,
  output q2,
  output q1,
  output q0
);

  D_Flip_Flop d_ff_1 (.D(d3), .clk(clk), .Q(q3), .preset(set), .reset(reset));  // open: Qn
  D_Flip_Flop d_ff_2 (.D(d2), .clk(clk), .Q(q1), .preset(set), .reset(reset));  // open: Qn
  Hex_Digit_Display hex_digit_display_1 (.value({q3, {2{q1}}, q0}));  // open: dp
  D_Flip_Flop d_ff_3 (.D(d1), .clk(clk), .Q(q1), .preset(set), .reset(reset));  // open: Qn
  D_Flip_Flop d_ff_4 (.D(d0), .clk(clk), .Q(q0), .preset(set), .reset(reset));  // open: Qn

  assign q2 = q1;
endmodule

module petzoid_accumulator_p227 (
  input  subtract,
  input  b3,
  input  b2,
  input  b1,
  input  b0,
  input  set,
  input  reset
);

  wire clk_out, signed_fourbit_adder_1_s0, signed_fourbit_adder_1_s1, signed_fourbit_adder_1_s2,
       signed_fourbit_adder_1_s3;
  wire [3:0] four_bit_latch_1_q0;

  signed_fourbit_adder signed_fourbit_adder_1 (
    .binv(subtract), .cin(subtract), .a0(four_bit_latch_1_q0[0]), .b0(b0), .a1(four_bit_latch_1_q0[1]),
    .b1(b1), .a2(four_bit_latch_1_q0[2]), .b2(b2), .a3(four_bit_latch_1_q0[3]), .b3(b3),
    .s0(signed_fourbit_adder_1_s0), .s1(signed_fourbit_adder_1_s1), .s2(signed_fourbit_adder_1_s2),
    .s3(signed_fourbit_adder_1_s3));  // open: cout
  Button clk (.out(clk_out));
  LED led_1 (.in(four_bit_latch_1_q0[3]));
  four_bit_latch four_bit_latch_1 (
    .d3(signed_fourbit_adder_1_s3), .d2(signed_fourbit_adder_1_s2), .d1(signed_fourbit_adder_1_s1),
    .d0(signed_fourbit_adder_1_s0), .set(set), .clk(clk_out), .reset(reset), .q3(four_bit_latch_1_q0[3]),
    .q2(four_bit_latch_1_q0[2]), .q1(four_bit_latch_1_q0[1]), .q0(four_bit_latch_1_q0[0]));
  LED led_2 (.in(four_bit_latch_1_q0[2]));
  LED led_3 (.in(four_bit_latch_1_q0[1]));
  LED led_4 (.in(four_bit_latch_1_q0[0]));
  Hex_Digit_Display hex_digit_display_1 (.value(four_bit_latch_1_q0));  // open: dp
endmodule

module freq_divider (
  input  enable,
  input  clear
);

  wire clock_1_out, d_ff_1_q, d_ff_1_qn;

  Clock clock_1 (.out(clock_1_out));
  D_Flip_Flop d_ff_1 (.D(d_ff_1_qn), .clk(clock_1_out), .Q(d_ff_1_q), .Qn(d_ff_1_qn));  // open: preset, reset
  // Digital_Oscilloscope digital_oscilloscope_1: pin names not known; wires that end beside it: clock_1_out, d_ff_1_q, enable, clear
endmodule
