// Logisim project clock.circ as structural Verilog: 7 circuits, main circuit main
module main (
);

  wire clock_1_out;
  wire [6:0] collection_1_ampm, collection_1_hour, collection_1_hour2, collection_1_min, collection_1_second,
       collection_1_tenmin, collection_1_tensecond;

  Clock clock_1 (.out(clock_1_out));
  collection collection_1 (
    .in_1(clock_1_out), .second(collection_1_second), .tensecond(collection_1_tensecond),
    .min(collection_1_min), .tenmin(collection_1_tenmin), .hour(collection_1_hour),
    .hour2(collection_1_hour2), .ampm(collection_1_ampm));
  _7_Segment_Display u_7_segment_display_1 (
    .g(collection_1_ampm[5]), .f(collection_1_ampm[1]), .a(collection_1_ampm[0]), .b(collection_1_ampm[6]),
    .e(collection_1_ampm[2]), .d(collection_1_ampm[3]), .c(collection_1_ampm[4]));  // open: dp
  _7_Segment_Display u_7_segment_display_2 (
    .g(collection_1_hour2[5]), .f(collection_1_hour2[1]), .a(collection_1_hour2[0]),
    .b(collection_1_hour2[6]), .e(collection_1_hour2[2]), .d(collection_1_hour2[3]), .c(collection_1_hour2[4]));  // open: dp
  _7_Segment_Display u_7_segment_display_3 (
    .g(collection_1_hour[5]), .f(collection_1_hour[1]), .a(collection_1_hour[0]), .b(collection_1_hour[6]),
    .e(collection_1_hour[2]), .d(collection_1_hour[3]), .c(collection_1_hour[4]));  // open: dp
  _7_Segment_Display u_7_segment_display_4 (
    .g(collection_1_tenmin[5]), .f(collection_1_tenmin[1]), .a(collection_1_tenmin[0]),
    .b(collection_1_tenmin[6]), .e(collection_1_tenmin[2]), .d(collection_1_tenmin[3]),
    .c(collection_1_tenmin[4]));  // open: dp
  _7_Segment_Display u_7_segment_display_5 (
    .g(collection_1_min[5]), .f(collection_1_min[1]), .a(collection_1_min[0]), .b(collection_1_min[6]),
    .e(collection_1_min[2]), .d(collection_1_min[3]), .c(collection_1_min[4]));  // open: dp
  _7_Segment_Display u_7_segment_display_6 (
    .g(collection_1_tensecond[5]), .f(collection_1_tensecond[1]), .a(collection_1_tensecond[0]),
    .b(collection_1_tensecond[6]), .e(collection_1_tensecond[2]), .d(collection_1_tensecond[3]),
    .c(collection_1_tensecond[4]));  // open: dp
  _7_Segment_Display u_7_segment_display_7 (
    .g(collection_1_second[5]), .f(collection_1_second[1]), .a(collection_1_second[0]),
    .b(collection_1_second[6]), .e(collection_1_second[2]), .d(collection_1_second[3]),
    .c(collection_1_second[4]));  // open: dp

  // Notes on the sheet:
  //   AM/PM INDICATOR
  //   Hour
  //   Min
  //   Sec
endmodule

module second (
  input  in_1,
  output out_2,
  output out_3,
  output out_4,
  output out_5,
  output out_6
);

  wire and_1_out, d_ff_1_qn, d_ff_2_qn, d_ff_3_qn, d_ff_4_qn;

  D_Flip_Flop d_ff_1 (.D(d_ff_1_qn), .clk(in_1), .Q(out_2), .Qn(d_ff_1_qn), .reset(and_1_out));  // open: preset
  D_Flip_Flop d_ff_2 (.D(d_ff_2_qn), .clk(d_ff_1_qn), .Q(out_3), .Qn(d_ff_2_qn), .reset(and_1_out));  // open: preset
  D_Flip_Flop d_ff_3 (.D(d_ff_3_qn), .clk(d_ff_2_qn), .Q(out_4), .Qn(d_ff_3_qn), .reset(and_1_out));  // open: preset
  D_Flip_Flop d_ff_4 (.D(d_ff_4_qn), .clk(d_ff_3_qn), .Q(out_5), .Qn(d_ff_4_qn), .reset(and_1_out));  // open: preset
  and and_1 (and_1_out, out_3, out_5);
  nand nand_1 (out_6, out_2, out_5);
endmodule

module Tensecandmin (
  input  in_1,
  output out_2,
  output out_3,
  output out_4,
  output out_5
);

  wire and_1_out, d_ff_1_qn, d_ff_2_qn, d_ff_3_qn;

  D_Flip_Flop d_ff_1 (.D(d_ff_1_qn), .clk(in_1), .Q(out_2), .Qn(d_ff_1_qn), .reset(and_1_out));  // open: preset
  D_Flip_Flop d_ff_2 (.D(d_ff_2_qn), .clk(d_ff_1_qn), .Q(out_3), .Qn(d_ff_2_qn), .reset(and_1_out));  // open: preset
  D_Flip_Flop d_ff_3 (.D(d_ff_3_qn), .clk(d_ff_2_qn), .Q(out_4), .Qn(d_ff_3_qn), .reset(and_1_out));  // open: preset
  and and_1 (and_1_out, out_3, out_4);
  nand nand_1 (out_5, out_2, out_4);
endmodule

module twehour (
  input  in_1,
  output out_2,
  output out_3,
  output out_4,
  output out_5,
  output out_6,
  output out_7
);

  wire and_1_out, and_2_out, d_ff_1_qn, d_ff_2_q, d_ff_2_qn, d_ff_3_qn, d_ff_4_qn, d_ff_5_q, d_ff_5_qn,
       d_ff_6_qn, nand_1_out, nand_2_out, nor_1_out, not_1_out, or_1_out;

  or or_1 (or_1_out, and_2_out, and_1_out);
  D_Flip_Flop d_ff_1 (.D(d_ff_1_qn), .clk(in_1), .Q(out_2), .Qn(d_ff_1_qn), .reset(or_1_out));  // open: preset
  D_Flip_Flop d_ff_2 (.D(d_ff_2_qn), .clk(d_ff_1_qn), .Q(d_ff_2_q), .Qn(d_ff_2_qn), .reset(or_1_out));  // open: preset
  D_Flip_Flop d_ff_3 (.D(d_ff_3_qn), .clk(d_ff_2_qn), .Q(out_4), .Qn(d_ff_3_qn), .reset(or_1_out));  // open: preset
  D_Flip_Flop d_ff_4 (.D(d_ff_4_qn), .clk(d_ff_3_qn), .Q(out_5), .Qn(d_ff_4_qn), .reset(or_1_out));  // open: preset
  and and_1 (and_1_out, d_ff_2_q, out_5);
  D_Flip_Flop d_ff_5 (
    .D(d_ff_5_qn), .clk(nand_1_out), .Q(d_ff_5_q), .Qn(d_ff_5_qn), .reset(and_2_out));  // open: preset
  nand nand_1 (nand_1_out, out_2, out_5);
  not not_1 (not_1_out, out_5);
  and and_2 (and_2_out, not_1_out, d_ff_2_q, d_ff_5_q);
  nor nor_1 (nor_1_out, d_ff_5_q, out_2, d_ff_2_q, out_4, out_5);
  nand nand_2 (nand_2_out, out_2, d_ff_5_q);
  or or_2 (out_3, d_ff_2_q, nor_1_out);
  D_Flip_Flop d_ff_6 (.D(d_ff_6_qn), .clk(nand_2_out), .Q(out_7), .Qn(d_ff_6_qn));  // open: preset, reset
  or or_3 (out_6, nor_1_out, d_ff_5_q);
endmodule

module binaryclock (
  input  in_1,
  output sec1,
  output sec2,
  output sec3,
  output sec4,
  output tensec1,
  output tensec2,
  output tensec3,
  output min1,
  output min2,
  output min3,
  output min4,
  output tenmin1,
  output tenmin2,
  output tenmin3,
  output hour1,
  output hour2,
  output hour3,
  output hour4,
  output hour5,
  output AMPM
);

  wire second_1_out_6, second_2_out_6, tensecandmin_1_out_5, tensecandmin_2_out_5;

  second second_1 (
    .in_1(tensecandmin_2_out_5), .out_2(min1), .out_3(min2), .out_4(min3), .out_5(min4),
    .out_6(second_1_out_6));
  Tensecandmin tensecandmin_1 (
    .in_1(second_1_out_6), .out_2(tenmin1), .out_3(tenmin2), .out_4(tenmin3), .out_5(tensecandmin_1_out_5));
  second second_2 (.in_1(in_1), .out_2(sec1), .out_3(sec2), .out_4(sec3), .out_5(sec4), .out_6(second_2_out_6));
  Tensecandmin tensecandmin_2 (
    .in_1(second_2_out_6), .out_2(tensec1), .out_3(tensec2), .out_4(tensec3), .out_5(tensecandmin_2_out_5));
  twehour twehour_1 (
    .in_1(tensecandmin_1_out_5), .out_2(hour1), .out_3(hour2), .out_4(hour3), .out_5(hour4), .out_6(hour5),
    .out_7(AMPM));
endmodule

module decodingciruity (
  input  in_1,
  input  in_2,
  input  in_3,
  input  in_4,
  output a,
  output b,
  output c,
  output d,
  output e,
  output f,
  output g
);

  wire and_1_out, and_2_out, and_3_out, and_4_out, and_5_out, and_6_out, and_8_out, and_9_out, and_10_out,
       not_1_out, not_2_out, not_3_out, not_4_out;

  not not_1 (not_1_out, in_1);
  not not_2 (not_2_out, in_2);
  not not_3 (not_3_out, in_3);
  not not_4 (not_4_out, in_4);
  and and_1 (and_1_out, not_1_out, not_2_out, not_3_out, not_4_out);
  and and_2 (and_2_out, not_1_out, not_2_out, not_3_out, in_4);
  and and_3 (and_3_out, not_1_out, not_2_out, in_3, not_4_out);
  and and_4 (and_4_out, not_1_out, not_2_out, in_3, in_4);
  and and_5 (and_5_out, not_1_out, in_2, not_3_out, not_4_out);
  and and_6 (and_6_out, not_1_out, in_2, not_3_out, in_4);
  and and_7 (and_6_out, not_1_out, in_2, not_3_out, in_4);
  and and_8 (and_8_out, not_1_out, in_2, in_3, not_4_out);
  and and_9 (and_9_out, not_1_out, in_2, in_3, in_4);
  and and_10 (and_10_out, in_1, not_2_out, not_3_out, not_4_out);
  // AND_Gate and_11 has open pins: in0=in_1, in1=not_2_out, in2=not_3_out, in3=in_4, out=open
  nor nor_1 (a, and_2_out, and_5_out);
  nor nor_2 (b, and_2_out, and_3_out, and_4_out, and_9_out);
  or or_1 (c, and_1_out, and_3_out, and_8_out, and_10_out);
  nor nor_3 (d, and_2_out, and_5_out, and_9_out);
  not not_5 (e, and_3_out);
  nor nor_4 (f, and_1_out, and_2_out, and_9_out);
  nor nor_5 (g, and_6_out, and_8_out);
endmodule

module collection (
  input  in_1,
  output [6:0] second,
  output [6:0] tensecond,
  output [6:0] min,
  output [6:0] tenmin,
  output [6:0] hour,
  output [6:0] hour2,
  output [6:0] ampm
);

  wire binaryclock_1_ampm, binaryclock_1_hour1, binaryclock_1_hour2, binaryclock_1_hour3,
       binaryclock_1_hour4, binaryclock_1_hour5, binaryclock_1_min1, binaryclock_1_min2, binaryclock_1_min3,
       binaryclock_1_min4, binaryclock_1_sec1, binaryclock_1_sec2, binaryclock_1_sec3, binaryclock_1_sec4,
       binaryclock_1_tenmin1, binaryclock_1_tenmin2, binaryclock_1_tenmin3, binaryclock_1_tensec1,
       binaryclock_1_tensec2, binaryclock_1_tensec3;

  binaryclock binaryclock_1 (
    .in_1(in_1), .sec1(binaryclock_1_sec1), .sec2(binaryclock_1_sec2), .sec3(binaryclock_1_sec3),
    .sec4(binaryclock_1_sec4), .tensec1(binaryclock_1_tensec1), .tensec2(binaryclock_1_tensec2),
    .tensec3(binaryclock_1_tensec3), .min1(binaryclock_1_min1), .min2(binaryclock_1_min2),
    .min3(binaryclock_1_min3), .min4(binaryclock_1_min4), .tenmin1(binaryclock_1_tenmin1),
    .tenmin2(binaryclock_1_tenmin2), .tenmin3(binaryclock_1_tenmin3), .hour1(binaryclock_1_hour1),
    .hour2(binaryclock_1_hour2), .hour3(binaryclock_1_hour3), .hour4(binaryclock_1_hour4),
    .hour5(binaryclock_1_hour5), .AMPM(binaryclock_1_ampm));
  decodingciruity decodingciruity_1 (
    .in_1(binaryclock_1_sec4), .in_2(binaryclock_1_sec3), .in_3(binaryclock_1_sec2),
    .in_4(binaryclock_1_sec1), .a(second[0]), .b(second[1]), .c(second[2]), .d(second[3]), .e(second[4]),
    .f(second[5]), .g(second[6]));
  decodingciruity decodingciruity_2 (
    .in_2(binaryclock_1_tensec3), .in_3(binaryclock_1_tensec2), .in_4(binaryclock_1_tensec1),
    .a(tensecond[0]), .b(tensecond[1]), .c(tensecond[2]), .d(tensecond[3]), .e(tensecond[4]),
    .f(tensecond[5]), .g(tensecond[6]));  // open: in_1
  decodingciruity decodingciruity_3 (
    .in_1(binaryclock_1_min4), .in_2(binaryclock_1_min3), .in_3(binaryclock_1_min2),
    .in_4(binaryclock_1_min1), .a(min[0]), .b(min[1]), .c(min[2]), .d(min[3]), .e(min[4]), .f(min[5]),
    .g(min[6]));
  decodingciruity decodingciruity_4 (
    .in_2(binaryclock_1_tenmin3), .in_3(binaryclock_1_tenmin2), .in_4(binaryclock_1_tenmin1), .a(tenmin[0]),
    .b(tenmin[1]), .c(tenmin[2]), .d(tenmin[3]), .e(tenmin[4]), .f(tenmin[5]), .g(tenmin[6]));  // open: in_1
  decodingciruity decodingciruity_5 (
    .in_1(binaryclock_1_hour4), .in_2(binaryclock_1_hour3), .in_3(binaryclock_1_hour2),
    .in_4(binaryclock_1_hour1), .a(hour[0]), .b(hour[1]), .c(hour[2]), .d(hour[3]), .e(hour[4]), .f(hour[5]),
    .g(hour[6]));
  decodingciruity decodingciruity_6 (
    .in_4(binaryclock_1_hour5), .a(hour2[0]), .b(hour2[1]), .c(hour2[2]), .d(hour2[3]), .e(hour2[4]),
    .f(hour2[5]), .g(hour2[6]));  // open: in_1, in_2, in_3
  decodingciruity decodingciruity_7 (
    .in_4(binaryclock_1_ampm), .a(ampm[0]), .b(ampm[1]), .c(ampm[2]), .d(ampm[3]), .e(ampm[4]), .f(ampm[5]),
    .g(ampm[6]));  // open: in_1, in_2, in_3
endmodule
